# Fritzing sketch Wiring_Diagram (saved by Fritzing 0.9.3b)
breadboards: 2

parts:
  Tiva_C_LaunchPad1 = Tiva C TM4C123G [package=THT]
  SG1 = Buzzer 12mm [package=buzzer-ccv]
  R1 = Photocell (LDR) [package=THT]
  R2 = Resistor [tolerance=±5% resistance=220 package="1206 [SMD]"]
  Part2 = SRF05 Ultrasonic Rangefinder
  Part3 = MQ-4
  S4 = Magnetic Door Switch [package=reed_switch_plastic]
  Part4 = Bluetooth HC-05 Macho
  Mod1 = KY-008 Laser Transmitter Module [package="Breakout board"]
  S5 = Momentary Switch [package=ksa_sealed_tac_switch]
  R3 = Resistor [tolerance=±5% resistance=220 package="1206 [SMD]"]
  Part5 = LCD1602-I2C
  Part1 = Arduino Uno (Rev3)

nets:
  VCC: Tiva_C_LaunchPad1.3.3V, Part2.VCC, Part3.VCC, Part4.VCC
  N1: Tiva_C_LaunchPad1.PE4, Part4.RXD
  N2: Tiva_C_LaunchPad1.PE5, Part4.TXD
  N3: Tiva_C_LaunchPad1.PA5, Mod1.S
  N4: Tiva_C_LaunchPad1.PD0, S4.2
  N5: Tiva_C_LaunchPad1.PE3, Part3.GND
  N6: Tiva_C_LaunchPad1.PC7, Part2.Echo
  N7: Tiva_C_LaunchPad1.PD6, Part2.Trig
  GND: Tiva_C_LaunchPad1.GND, Part2.GND, Part3.AO, S4.1, Part4.GND
  GND_2: SG1.1, R2.Pin_1, Mod1.-, R3.Pin_1, Part5.GND, Part1.GND
  N8: SG1.2, Part1.D7
  N9: R1.pin_0, Part1.A0
  N10: R1.pin_1, R2.Pin_0
  VCC_2: Mod1.NC, Part5.VCC, Part1.5V
  N11: S5.1, Part1.D2
  N12: S5.4, R3.Pin_0
  N13: Part5.SDA, Part1.A4/SDA
  N14: Part5.SCL, Part1.A5/SCL

notes:
  TIVA-C Micro Controller "TM4C123G"
  Ultrasonic Sensor
  Fume Sensor
  Bluetooth Transmitter
  Magnetic Door Switch
  LCD Display
  Arduino
  Buzzer 12mm
  Laser Transmitter
  PhotoCell (LDR)
  Mute PB
  Laser

custom parts:
  Tiva C TM4C123G: Tiva C LaunchPad EK-TM4C123GXL
  KY-008 Laser Transmitter Module: KY-008 Laser Transmitter Module, emits a dot shaped red laser beam.
  LCD1602-I2C: A standard character display, usually with 2x16 characters. Comes in many colors with LCM1602 IIC attached.
